// Logisim project Guess The Number.circ as structural Verilog: 13 circuits, main circuit seletor
module main (
  input  in_1,
  input  in_2,
  input  in_3,
  input  in_4,
  input  in_5,
  input  in_6,
  input  in_7,
  input  in_8,
  input  Jogador,
  input  Jogar
);

  wire decode_1_out_5, decode_1_out_6, decode_1_out_7, decode_1_out_8, decode_1_out_9, decode_1_out_10,
       decode_1_out_11, decode_2_out_5, decode_2_out_6, decode_2_out_7, decode_2_out_8, decode_2_out_9,
       decode_2_out_10, decode_2_out_11, game_1_out_11, game_1_out_12, game_1_out_13;

  _7_Segment_Display u_7_segment_display_1 (
    .g(decode_1_out_8), .f(decode_1_out_7), .a(decode_1_out_6), .b(decode_1_out_5), .e(decode_1_out_11),
    .d(decode_1_out_10), .c(decode_1_out_9));  // open: dp
  _7_Segment_Display u_7_segment_display_2 (
    .g(decode_2_out_8), .f(decode_2_out_7), .a(decode_2_out_6), .b(decode_2_out_5), .e(decode_2_out_11),
    .d(decode_2_out_10), .c(decode_2_out_9));  // open: dp
  decode decode_1 (
    .C3(in_1), .C2(in_2), .C1(in_3), .C0(in_4), .out_5(decode_1_out_5), .out_6(decode_1_out_6),
    .out_7(decode_1_out_7), .out_8(decode_1_out_8), .out_9(decode_1_out_9), .out_10(decode_1_out_10),
    .out_11(decode_1_out_11));
  decode decode_2 (
    .C3(in_5), .C2(in_6), .C1(in_7), .C0(in_8), .out_5(decode_2_out_5), .out_6(decode_2_out_6),
    .out_7(decode_2_out_7), .out_8(decode_2_out_8), .out_9(decode_2_out_9), .out_10(decode_2_out_10),
    .out_11(decode_2_out_11));
  game game_1 (
    .A3(in_1), .A2(in_2), .A1(in_3), .A0(in_4), .B3(in_5), .B2(in_6), .B1(in_7), .B0(in_8),
    .Jogador(Jogador), .Jogar(Jogar), .out_11(game_1_out_11), .out_12(game_1_out_12), .out_13(game_1_out_13));
  LED led_1 (.in(game_1_out_11));
  LED led_2 (.in(game_1_out_12));
  LED led_3 (.in(game_1_out_13));

  // Notes on the sheet:
  //   Menor
  //   Acertou
  //   Maior
endmodule

module seletor (
  input  C,
  input  A,
  input  B,
  output S
);

  wire and_1_out, and_2_out, not_1_out;

  not not_1 (not_1_out, C);
  and and_1 (and_1_out, C, B);
  and and_2 (and_2_out, A, not_1_out);
  or or_1 (S, and_1_out, and_2_out);
endmodule

module XNOR (
  input  A,
  input  B,
  output S
);

  wire and_1_out, and_2_out, not_1_out, not_2_out;

  not not_1 (not_1_out, A);
  and and_1 (and_1_out, not_1_out, not_2_out);
  not not_2 (not_2_out, B);
  and and_2 (and_2_out, A, B);
  or or_1 (S, and_1_out, and_2_out);
endmodule

module game (
  input  A3,
  input  A2,
  input  A1,
  input  A0,
  input  B3,
  input  B2,
  input  B1,
  input  B0,
  input  Jogador,
  input  Jogar,
  output out_11,
  output out_12,
  output out_13
);

  wire comparador_1_out_5, comparador_1_out_6, comparador_1_out_7, seletor_1_s, seletor_2_s, seletor_3_s,
       seletor_4_s;

  seletor seletor_1 (.C(Jogador), .A(A3), .B(B3), .S(seletor_1_s));
  seletor seletor_2 (.C(Jogador), .A(A2), .B(B2), .S(seletor_2_s));
  seletor seletor_3 (.C(Jogador), .A(A1), .B(B1), .S(seletor_3_s));
  seletor seletor_4 (.C(Jogador), .A(A0), .B(B0), .S(seletor_4_s));
  Comparador comparador_1 (
    .A3(seletor_1_s), .A2(seletor_2_s), .A1(seletor_3_s), .A0(seletor_4_s), .out_5(comparador_1_out_5),
    .out_6(comparador_1_out_6), .out_7(comparador_1_out_7));
  and and_1 (out_11, Jogar, comparador_1_out_5);
  and and_2 (out_12, Jogar, comparador_1_out_6);
  and and_3 (out_13, Jogar, comparador_1_out_7);
endmodule

module Comparador (
  input  A3,
  input  A2,
  input  A1,
  input  A0,
  output out_5,
  output out_6,
  output out_7
);

  wire and_1_out, and_2_out, and_3_out, and_4_out, and_5_out, and_6_out, and_7_out, not_1_out, not_2_out,
       not_3_out, not_4_out, not_5_out, not_6_out, xnor_1_s, xnor_2_s, xnor_3_s, xnor_4_s;

  not not_1 (not_1_out, 1'b0);
  and and_1 (and_1_out, A0, not_1_out);
  not not_2 (not_2_out, 1'b1);
  and and_2 (and_2_out, A2, not_3_out);
  not not_3 (not_3_out, 1'b1);
  not not_4 (not_4_out, 1'b0);
  XNOR xnor_1 (.A(A1), .B(1'b1), .S(xnor_1_s));
  and and_3 (and_3_out, A1, not_2_out);
  XNOR xnor_2 (.A(1'b1), .B(A2), .S(xnor_2_s));
  and and_4 (and_4_out, A3, not_4_out);
  and and_5 (and_5_out, and_1_out, xnor_1_s, xnor_2_s, xnor_3_s);
  XNOR xnor_3 (.A(1'b0), .B(A3), .S(xnor_3_s));
  and and_6 (and_6_out, and_3_out, xnor_2_s, xnor_3_s);
  and and_7 (and_7_out, and_2_out, xnor_3_s);
  XNOR xnor_4 (.A(A0), .B(1'b0), .S(xnor_4_s));
  and and_8 (out_6, xnor_1_s, xnor_2_s, xnor_3_s, xnor_4_s);
  or or_1 (out_7, and_5_out, and_6_out, and_7_out, and_4_out);
  not not_5 (not_5_out, out_6);
  and and_9 (out_5, not_5_out, not_6_out);
  not not_6 (not_6_out, out_7);
endmodule

module decode (
  input  C3,
  input  C2,
  input  C1,
  input  C0,
  output out_5,
  output out_6,
  output out_7,
  output out_8,
  output out_9,
  output out_10,
  output out_11
);

  SEG1 seg1_1 (.C3(C3), .C2(C2), .C1(C1), .C0(C0), .out_5(out_5));
  SEG2 seg2_1 (.C3(C3), .C2(C2), .C1(C1), .C0(C0), .out_5(out_6));
  SEG3 seg3_1 (.C3(C3), .C2(C2), .C1(C1), .C0(C0), .out_5(out_7));
  SEG4 seg4_1 (.C3(C3), .C2(C2), .C1(C1), .C0(C0), .out_5(out_8));
  SEG5 seg5_1 (.C3(C3), .C2(C2), .C1(C1), .C0(C0), .out_5(out_9));
  SEG6 seg6_1 (.C3(C3), .C2(C2), .C1(C1), .C0(C0), .out_5(out_10));
  SEG7 seg7_1 (.C3(C3), .C2(C2), .C1(C1), .C0(C0), .out_5(out_11));
endmodule

module SEG2 (
  input  C3,
  input  C2,
  input  C1,
  input  C0,
  output out_5
);

  wire and_1_out, and_2_out, and_3_out, and_4_out, and_5_out, and_6_out, and_7_out, not_1_out, not_2_out,
       not_3_out, not_4_out, not_5_out, not_6_out;

  not not_1 (not_1_out, C0);
  not not_2 (not_2_out, C3);
  not not_3 (not_3_out, C2);
  not not_4 (not_4_out, C2);
  not not_5 (not_5_out, C1);
  not not_6 (not_6_out, C0);
  and and_1 (and_1_out, C1, not_1_out);
  and and_2 (and_2_out, C2, C1, C0);
  and and_3 (and_3_out, not_2_out, C1, C0);
  and and_4 (and_4_out, not_2_out, C2, C0);
  and and_5 (and_5_out, C3, not_3_out, not_5_out);
  and and_6 (and_6_out, C3, not_5_out, not_6_out);
  and and_7 (and_7_out, not_4_out, not_5_out, not_6_out);
  or or_1 (out_5, and_1_out, and_2_out, and_3_out, and_4_out, and_5_out, and_6_out, and_7_out);
endmodule

module SEG1 (
  input  C3,
  input  C2,
  input  C1,
  input  C0,
  output out_5
);

  wire and_1_out, and_2_out, and_3_out, and_4_out, and_5_out, not_1_out, not_2_out, not_3_out, not_4_out;

  not not_1 (not_1_out, C2);
  not not_2 (not_2_out, C3);
  not not_3 (not_3_out, C1);
  not not_4 (not_4_out, C0);
  and and_1 (and_1_out, not_2_out, not_1_out);
  and and_2 (and_2_out, C3, not_3_out, C0);
  and and_3 (and_3_out, C3, not_1_out, not_4_out);
  and and_4 (and_4_out, not_2_out, C1, C0);
  and and_5 (and_5_out, not_2_out, not_3_out, not_4_out);
  or or_1 (out_5, and_1_out, and_2_out, and_3_out, and_4_out, and_5_out);
endmodule

module SEG3 (
  input  C3,
  input  C2,
  input  C1,
  input  C0,
  output out_5
);

  wire and_1_out, and_2_out, and_3_out, and_4_out, and_5_out, not_1_out, not_2_out, not_3_out, not_4_out;

  not not_1 (not_1_out, C2);
  not not_2 (not_2_out, C3);
  not not_3 (not_3_out, C1);
  not not_4 (not_4_out, C0);
  and and_1 (and_1_out, not_3_out, not_4_out);
  and and_2 (and_2_out, C3, not_1_out);
  and and_3 (and_3_out, not_2_out, C2, not_3_out);
  and and_4 (and_4_out, C3, C2, C1);
  and and_5 (and_5_out, C2, C1, not_4_out);
  or or_1 (out_5, and_1_out, and_2_out, and_3_out, and_4_out, and_5_out);
endmodule

module SEG4 (
  input  C3,
  input  C2,
  input  C1,
  input  C0,
  output out_5
);

  wire and_1_out, and_2_out, and_3_out, and_4_out, and_5_out, not_1_out, not_2_out, not_3_out, not_4_out;

  not not_1 (not_1_out, C2);
  not not_2 (not_2_out, C3);
  not not_3 (not_3_out, C1);
  not not_4 (not_4_out, C0);
  and and_1 (and_1_out, C3, not_1_out);
  and and_2 (and_2_out, C3, C2, C0);
  and and_3 (and_3_out, not_2_out, C2, not_3_out);
  and and_4 (and_4_out, not_2_out, not_1_out, C1);
  and and_5 (and_5_out, C1, not_4_out);
  or or_1 (out_5, and_1_out, and_2_out, and_3_out, and_4_out, and_5_out);
endmodule

module SEG5 (
  input  C3,
  input  C2,
  input  C1,
  input  C0,
  output out_5
);

  wire and_1_out, and_2_out, and_3_out, and_4_out, and_5_out, not_1_out, not_2_out, not_3_out, not_4_out;

  not not_1 (not_1_out, C2);
  not not_2 (not_2_out, C3);
  not not_3 (not_3_out, C0);
  not not_4 (not_4_out, C1);
  and and_1 (and_1_out, C3, not_1_out);
  and and_2 (and_2_out, not_2_out, C2);
  and and_3 (and_3_out, not_2_out, C1, C0);
  and and_4 (and_4_out, not_2_out, not_4_out, not_3_out);
  and and_5 (and_5_out, not_4_out, C0);
  or or_1 (out_5, and_1_out, and_2_out, and_3_out, and_4_out, and_5_out);
endmodule

module SEG6 (
  input  C3,
  input  C2,
  input  C1,
  input  C0,
  output out_5
);

  wire and_1_out, and_2_out, and_3_out, and_4_out, and_5_out, and_6_out, not_1_out, not_2_out, not_3_out,
       not_4_out;

  not not_1 (not_1_out, C1);
  not not_2 (not_2_out, C3);
  not not_3 (not_3_out, C2);
  not not_4 (not_4_out, C0);
  and and_1 (and_1_out, C3, C2, not_1_out);
  and and_2 (and_2_out, not_2_out, not_3_out, C1);
  and and_3 (and_3_out, C3, not_3_out, C0);
  and and_4 (and_4_out, C2, C1, not_4_out);
  and and_5 (and_5_out, C2, not_1_out, C0);
  and and_6 (and_6_out, not_3_out, not_1_out, not_4_out);
  or or_1 (out_5, and_1_out, and_2_out, and_3_out, and_4_out, and_5_out, and_6_out);
endmodule

module SEG7 (
  input  C3,
  input  C2,
  input  C1,
  input  C0,
  output out_5
);

  wire and_1_out, and_2_out, and_3_out, and_4_out, not_1_out, not_2_out, not_3_out;

  not not_1 (not_1_out, C2);
  not not_2 (not_2_out, C1);
  not not_3 (not_3_out, C0);
  and and_1 (and_1_out, C3, C2);
  and and_2 (and_2_out, C3, C1, C0);
  and and_3 (and_3_out, not_1_out, not_2_out, not_3_out);
  and and_4 (and_4_out, C1, not_3_out);
  or or_1 (out_5, and_1_out, and_2_out, and_3_out, and_4_out);
endmodule
